// Logisim project MorseCode.circ as structural Verilog: 1 circuit, main circuit main
module main (
  input  [1:0] in_1,
  input  [1:0] in_2,
  input  in_3
);

  wire A_prime_B_prime_2_out, A_prime_B_prime_out, A_prime_C_prime_D_prime_out, and_1_out,
       B_prime_C_prime_2_out, B_prime_C_prime_D_out, B_prime_C_prime_out, B_prime_D_prime_out, BC_out,
       BCD_out, clock_1_out, not_1_out, not_2_out, not_3_out, not_4_out, not_5_out, not_6_out, not_7_out,
       not_8_out, not_9_out, not_10_out, not_11_out, not_12_out, not_13_out, not_14_out, not_15_out,
       not_16_out, not_17_out, not_18_out, or_1_out, or_2_out, or_3_out, or_4_out, or_5_out;
  wire [3:0] adder_1_out, divider_1_rem, register_1_q;

  Adder #(.width(4)) adder_1 (.a(register_1_q), .b({in_2, in_1}), .out(adder_1_out));  // open: cin, cout
  Divider #(.width(4)) divider_1 (.a(adder_1_out), .b(4'b1010), .rem(divider_1_rem));  // open: out, upper
  Clock clock_1 (.out(clock_1_out));
  Register #(.width(4)) register_1 (.D(divider_1_rem), .en(in_3), .Q(register_1_q), .clk(clock_1_out));  // open: clr
  Hex_Digit_Display hex_digit_display_1 (.value(register_1_q));  // open: dp
  not not_1 (not_1_out, register_1_q[0]);
  not not_2 (not_2_out, register_1_q[1]);
  not not_3 (not_3_out, register_1_q[2]);
  not not_4 (not_4_out, register_1_q[1]);
  not not_5 (not_5_out, register_1_q[2]);
  not not_6 (not_6_out, register_1_q[1]);
  not not_7 (not_7_out, register_1_q[2]);
  not not_8 (not_8_out, register_1_q[0]);
  not not_9 (not_9_out, register_1_q[2]);
  not not_10 (not_10_out, register_1_q[2]);
  not not_11 (not_11_out, register_1_q[3]);
  not not_12 (not_12_out, register_1_q[1]);
  not not_13 (not_13_out, register_1_q[2]);
  not not_14 (not_14_out, register_1_q[2]);
  not not_15 (not_15_out, register_1_q[3]);
  not not_16 (not_16_out, register_1_q[3]);
  not not_17 (not_17_out, register_1_q[1]);
  not not_18 (not_18_out, register_1_q[0]);
  and and_1 (and_1_out, not_1_out, not_2_out, not_3_out);
  and BC (BC_out, register_1_q[1], register_1_q[2]);
  and B_prime_C_prime (B_prime_C_prime_out, not_4_out, not_5_out);
  and BCD (BCD_out, register_1_q[0], register_1_q[1], register_1_q[2]);
  and B_prime_C_prime_2 (B_prime_C_prime_2_out, not_6_out, not_7_out);
  and B_prime_D_prime (B_prime_D_prime_out, not_8_out, not_9_out);
  and A_prime_B_prime (A_prime_B_prime_out, not_10_out, not_11_out);
  and B_prime_C_prime_D (B_prime_C_prime_D_out, register_1_q[0], not_12_out, not_13_out);
  and A_prime_B_prime_2 (A_prime_B_prime_2_out, not_14_out, not_15_out);
  and A_prime_C_prime_D_prime (A_prime_C_prime_D_prime_out, not_16_out, not_17_out, not_18_out);
  or or_1 (or_1_out, and_1_out, register_1_q[3], BC_out);
  or or_2 (or_2_out, B_prime_C_prime_out, BCD_out);
  or or_3 (or_3_out, B_prime_C_prime_2_out, B_prime_D_prime_out);
  or or_4 (or_4_out, A_prime_B_prime_out, B_prime_C_prime_D_out);
  or or_5 (or_5_out, A_prime_B_prime_2_out, A_prime_C_prime_D_prime_out);
  LED led_1 (.in(or_1_out));
  LED led_2 (.in(or_2_out));
  LED led_3 (.in(or_3_out));
  LED led_4 (.in(or_4_out));
  LED led_5 (.in(or_5_out));

  // Notes on the sheet:
  //   Left
  //   B'C'D'
  //   A
  //   Center Left
  //   Center
  //   Center Right
  //   Right
endmodule
