// Logisim project primes.circ as structural Verilog: 1 circuit, main circuit main
module main (
  input  [2:0] in_1,
  input  [2:0] in_2
);

  wire and_1_out, and_2_out, and_3_out, and_4_out, comparator_1_eq, comparator_2_eq, not_1_out, not_2_out,
       not_3_out, not_4_out, or_1_out, xnor_1_out, xor_1_out;
  wire [3:0] adder_1_out, bit_extender_1_out, bit_extender_2_out, divider_1_rem, divider_2_rem;

  assign bit_extender_1_out = {{1{1'b0}}, in_1};  // Bit_Extender bit_extender_1
  assign bit_extender_2_out = {{1{1'b0}}, in_2};  // Bit_Extender bit_extender_2
  Hex_Digit_Display hex_digit_display_1 (.value(adder_1_out));  // open: dp
  Adder #(.width(4)) adder_1 (.a(bit_extender_1_out), .b(bit_extender_2_out), .out(adder_1_out));  // open: cin, cout
  not not_1 (not_1_out, adder_1_out[3]);
  not not_2 (not_2_out, adder_1_out[2]);
  Divider #(.width(4)) divider_1 (.a(adder_1_out), .b(4'b0011), .rem(divider_1_rem));  // open: out, upper
  Divider #(.width(4)) divider_2 (.a(adder_1_out), .b(4'b0010), .rem(divider_2_rem));  // open: out, upper
  not not_3 (not_3_out, adder_1_out[0]);
  not not_4 (not_4_out, adder_1_out[1]);
  Comparator #(.width(4)) comparator_1 (.a(divider_1_rem), .b(4'b0000), .eq(comparator_1_eq));  // open: gt, lt
  Comparator #(.width(4)) comparator_2 (.a(divider_2_rem), .b(4'b0000), .eq(comparator_2_eq));  // open: gt, lt
  and and_1 (and_1_out, not_4_out, adder_1_out[0], not_2_out, not_1_out);
  and and_2 (and_2_out, not_3_out, adder_1_out[1], not_2_out, not_1_out);
  and and_3 (and_3_out, adder_1_out[0], adder_1_out[1], not_2_out, not_1_out);
  xnor xnor_1 (xnor_1_out, comparator_1_eq, comparator_2_eq);
  and and_4 (and_4_out, comparator_1_eq, comparator_2_eq);
  ExactlyOne xor_1 (.out(xor_1_out), .in1(and_1_out), .in2(xnor_1_out), .in3(and_4_out));
  LED led_1 (.in(or_1_out));
  or or_1 (or_1_out, xor_1_out, and_2_out, and_3_out);
endmodule
